# Fritzing sketch NewLIRADiagram (saved by Fritzing 0.9.3b)
# 18650 Li-ion Battery: CC-BY Dr Kristofer Chan, King's College London/Remote-research.org
breadboards: 1

parts:
  A1 = u-blox NEO-6M GPS Breakout
  MCU1 = Raspberry Pi Zero
  Part1 = USB converter CP2102
  TP1 = TP4056 [chip_label=TP4056 package="DIP (Dual Inline) [THT]"]
  U1 = LIPO-2000mAh [package=lipo-2000]
  BAT1 = 18650 Li-ion Battery [package=battery-18650]
  Buck_Convertor1 = Buck Convertor [part_number=LM2596 package=THT]
  Q1 = NPN-Transistor [package="SOT-23 [SMD]"]
  SG1 = Buzzer 12mm [package=buzzer-12mm-ns]
  R1 = Resistor [tolerance=±5% resistance=1000 package=THT]
  R2 = Resistor [tolerance=±5% resistance=2000 package=THT]
  Mod1 = KY-016 RGB Full Color LED Module [package="Breakout board"]
  S1 = Pushbutton [package="[SMD]"]
  Power_White_LED1 = White LED
  Q2 = NPN-Transistor [package="SOT-23 [SMD]"]
  U2 = LM2596 step down module
  TP2 = TP4056 [chip_label=TP4056 package="DIP (Dual Inline) [THT]"]
  SIM800L_BO1 = SIM800L BO

nets:
  N1: A1.Pin_1, Part1.+5V, TP1.pin4, TP1.pin5, U1.-, Buck_Convertor1.Positive_Input, R1.Pin_1, Q2.2, U2.IN+
  N2: A1.Pin_2, MCU1.pin_6, MCU1.pin_39, U1.+, Buck_Convertor1.Negative_Input, SG1.1, Mod1.-, S1.Pin_1, S1.Pin_2, Power_White_LED1.White_-, U2.IN-, U2.OUT-
  N3: A1.Pin_3, MCU1.pin_10, MCU1.pin_12
  N4: A1.Pin_4, MCU1.pin_8
  N5: MCU1.pin_13, Q1.0
  N6: MCU1.pin_15, Mod1.R
  N7: MCU1.pin_16, Mod1.B
  N8: MCU1.pin_18, Mod1.G
  N9: MCU1.pin_22, S1.Pin_3, S1.Pin_4
  N10: MCU1.pin_37, Q2.0
  N11: Part1.TXO, R2.Pin_0
  N12: Part1.RXI, SIM800L_BO1.PIN3
  N13: BAT1.-, TP2.pin3
  N14: BAT1.+, TP2.pin5, TP2.pin6
  N15: Buck_Convertor1.Negative_Output, SIM800L_BO1.pin_12
  N16: Buck_Convertor1.Positive_Output, SIM800L_BO1.pin_5
  N17: Q1.2, SG1.2
  N18: Q1.1, U2.OUT+
  N19: R1.Pin_0, R2.Pin_1, SIM800L_BO1.PIN1
  N20: Power_White_LED1.White_+, Q2.1

notes:
  USB to Micro USB (USB Cord) to Power Raspberry Pi
  QC4.0 QC3.0 LED Dual USB 5V 4.5A 22.5W Micro/Type-C USB 18650 Charging Module Temperature / Circuit Protection
  MICRO USB-TO-USB ADAPTER

custom parts:
  TP4056: A DIP stand-in part for whatever IC you want. With 6 pins on a 300mil dual inline package (DIP) footprint.
  18650 Li-ion Battery: 18650 li-ion Battery Standard 18650 battery with interactive connectors Creative Common Attribution 4.0 International (CC-BY 4.0) license. Any use of this part requires attribution of Dr Kristofer Chan, Department of Geography, King's College London. Contact kristofer.chan [at] kcl.ac.uk OR kris [at] remote-research.org for further information.
  Buck Convertor: DC to DC buck convertor
  KY-016 RGB Full Color LED Module: KY-016 Arduino full color 5mm RGB LED, different colors can be obtained by mixing the three primary colors.
  White LED: Testing
  LM2596 step down module: LM2596 DC-DC step down power supply module 3 A.
