# Fritzing sketch lira_schematic (saved by Fritzing 0.9.3b)
breadboards: 2

parts:
  S1 = Pushbutton [package="[SMD]"]
  R2 = Resistor [tolerance=±5% resistance=10 package="0603 [SMD]"]
  Arduino_Mega1 = Arduino Mega ADK (Rev3)
  Voice_Recognition1 = elechouse_voice_recognition_module_v3
  LED2 = smd LED [color="Red (633nm)" package="1206 [SMD]"]
  R4 = Resistor [tolerance=±5% resistance=10 package="0603 [SMD]"]
  R5 = Resistor [tolerance=±5% resistance=10 package="0603 [SMD]"]
  R6 = Resistor [tolerance=±5% resistance=10 package="0603 [SMD]"]
  S2 = Pushbutton [package="[SMD]"]
  GPS_Module_Ublox_NEO-6M1 = u-blox NEO-6M GPS Breakout
  Speaker1 = SPEAKER [package=pcb_mount_speaker]
  SIM800L2 = SIM800L
  YwRobot_Power_Supply1 = YwRobot Breadboard Power Supply [part_number=545043]
  R7 = Resistor [tolerance=±5% resistance=2.2k package="0603 [SMD]"]
  MCU1 = Raspberry Pi Zero
  YwRobot_Power_Supply2 = YwRobot Breadboard Power Supply [part_number=545043]
  SIM800C1 = SIM800C
  SP1 = SPEAKER [package=pcb_mount_speaker]
  MIC1 = Microphone
  GY-NEO6MV3 = SUP500F [package=sup500f]
  Mod1 = KY-016 RGB Full Color LED Module [package="Breakout board"]

nets:
  N1: S1.Pin_1, S1.Pin_2, YwRobot_Power_Supply2.VCC#9
  N2: S1.Pin_3, S1.Pin_4, R2.Pin_0
  N3: R2.Pin_1, MCU1.pin_14, MCU1.pin_39, SIM800C1.GND#6, GY-NEO6MV3.GND, Mod1.-
  N4: Arduino_Mega1.D19/RX1, Voice_Recognition1.TXD
  N5: Arduino_Mega1.D18/TX1, Voice_Recognition1.RXD
  N6: Arduino_Mega1.D17/RX2, GPS_Module_Ublox_NEO-6M1.Pin_3
  N7: Arduino_Mega1.D16/TX2, GPS_Module_Ublox_NEO-6M1.Pin_4
  GND: Arduino_Mega1.GND, Voice_Recognition1.GND, LED2.cathode, R5.Pin_0, GPS_Module_Ublox_NEO-6M1.Pin_2, Speaker1.+, R7.Pin_0
  N8: Arduino_Mega1.D9_PWM, Speaker1.-
  N9: Arduino_Mega1.D8_PWM, R5.Pin_1, S2.Pin_3, S2.Pin_4
  N10: Arduino_Mega1.D0/RX0, SIM800L2.TXD
  N11: Arduino_Mega1.D1/TX0, R4.Pin_0
  N12: Arduino_Mega1.D7_PWM, R6.Pin_1
  N13: Voice_Recognition1.VCC, S2.Pin_1, S2.Pin_2, YwRobot_Power_Supply1.VCC#5
  N14: LED2.anode, R6.Pin_0
  N15: R4.Pin_1, SIM800L2.RXD, R7.Pin_1
  N16: GPS_Module_Ublox_NEO-6M1.Pin_1, SIM800L2.VCC, YwRobot_Power_Supply1.VCC#9
  N17: YwRobot_Power_Supply2.VCC#5, GY-NEO6MV3.VCC
  N18: SIM800C1.SPKN, SP1.+
  N19: SIM800C1.SPKP, SP1.-
  N20: SIM800C1.MCN, MIC1.pin1
  N21: SIM800C1.MCP, MIC1.pin2
  N22: SIM800C1.GND#13, SIM800C1.PWX

notes:
  3 volts
  5 volts
  Convert to 3 Volt
  Use for texting
  Use to generate random lights
  Use to locate the current location
  Use as extra power supply
  Button use to do command
  This microcontroller handle voice recognition and speaker.
  MUST: Voltage must be 3.7-4.7 volts

custom parts:
  elechouse_voice_recognition_module_v3: Elechouse voice recognition module v3. Module that accepts up to 7 voice commands via a microphone. Note: currently this part was made from a .png image of the board. Thus the pcb is probably not correctly dimensioned since the input data was not precise. Before making boards based on this part, print out the footprint and check it (and provide corrections via the Fritzing forums to correct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
  SIM800L: SIM800L is a miniature cellular module which allows for GPRS transmission, sending and receiving SMS and making and receiving voice calls. Low cost and small footprint and quad band frequency support make this module perfect solution for any project that require long range connectivity. After connecting power module boots up, searches for cellular network and login automatically. On board LED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
  YwRobot Breadboard Power Supply: The YwRobot Breadboard Power Supply (MB-V2) has two power rails; they can be 5V or 3V3. Power to the module can be provided through the female USB socket or through the A10 (female) 2.1mm power jack.
  KY-016 RGB Full Color LED Module: KY-016 Arduino full color 5mm RGB LED, different colors can be obtained by mixing the three primary colors.
